# Fritzing sketch combo (saved by Fritzing 0.9.3b)
breadboards: 1

parts:
  Part1 = Arduino Mega 2560 (Rev3)
  R1 = Temperature Sensor (Thermistor) [thermistor_type=NTC package=THT]
  R2 = Resistor [tolerance=±5% resistance=10k package="2512 [SMD]"]
  R3 = PHOTOCELL [package=photocell-kit]
  R4 = Resistor [tolerance=±5% resistance=10k package="2512 [SMD]"]
  LED1 = smd LED [color="Red (633nm)" package="1206 [SMD]"]
  R5 = Resistor [tolerance=±5% resistance=3.3k package="1206 [SMD]"]

nets:
  N1: Part1.A0, R1.pin_0, R2.Pin_1
  N2: Part1.A7, R3.P$1, R4.Pin_1
  N3: Part1.5V, R1.pin_1, R3.P$2, R4.Pin_0
  N4: Part1.GND, R2.Pin_0, R5.Pin_0
  N5: Part1.D22, LED1.anode
  N6: LED1.cathode, R5.Pin_1
